# Fritzing sketch умный дом (saved by Fritzing 0.9.3b)

parts:
  Часть1 = Arduino Mega 2560 (Rev3)
  U1 = ESP8266 WiFi Module [part_number=ESP8266]
  LED1 = LED - 5mm [color="Red (633nm)" package="5 mm [THT]"]
  R1 = Resistor [tolerance=±5% resistance=220 package=THT]
  R2 = Resistor [tolerance=±5% resistance=100 package=THT]  # not connected
  R3 = Resistor [tolerance=±5% resistance=10k package=THT]
  U2 = Voltage Regulator - 3.3V [package="TO220 [THT]"]
  LED2 = LEDs [package=led10mm]
  U3 = LIPO-110mAh [package=lipo-110]
  M1 = DC Motor
  Q2 = Basic FET N-Channel [package="TO220 [THT]"]
  R4 = Resistor [tolerance=±5% resistance=10k package=THT]
  R5 = Resistor [tolerance=±5% resistance=100 package=THT]
  Q3 = Basic FET N-Channel [package="TO220 [THT]"]
  J1 = Basic Servo

nets:
  N1: Часть1.D19/RX1, U1.TXD
  N2: Часть1.D18/TX1, U1.RXD
  N3: Часть1.GND, LED1.cathode, R5.Pin_0, Q3.source
  N4: Часть1.D12_PWM, R1.Pin_1
  N5: Часть1.D8_PWM, J1.pulse
  N6: Часть1.D6_PWM, R3.Pin_1
  N7: Часть1.D7_PWM, R4.Pin_1
  N8: U1.VCC, U2.output_voltage
  N9: R3.Pin_0, Q3.gate
  N10: U2.input_voltage, U3.+
  N11: U2.GND, U3.-
  N12: LED2.C, Q3.drain
  N13: M1.pin_1, Q2.drain

notes:
  By Egor Duplin
  cleverHome
